# Fritzing sketch estacion-de-autos (saved by Fritzing 0.9.3b)
breadboards: 1

parts:
  part = Arduino Nano (Rev3.0)
  Display_de_7_segmentos = 7 Segment Display
  M1 = DC Motor
  S1 = Reed switch [package=THT]
  Tiras_de_LEDs_en_los_3_pisos = SMD RGB LED (WS2812) [package=5050]
  Piso_1 = SWITCH-MOMENTARY-2 [package=tactile-pth]
  Buzzer = Piezo Speaker
  Piso_2 = SWITCH-MOMENTARY-2 [package=tactile-pth]
  Piso_3 = SWITCH-MOMENTARY-2 [package=tactile-pth]
  S2 = Reed switch [package=THT]
  S3 = Reed switch [package=THT]
  D1 = LED - 5mm [color="Green (555nm)" package="5 mm [THT]"]
  U1 = L298 [package=multiwatt15_6400bgheatsink]
  IC1 = Voltage Regulator [package=78xxl]

nets:
  GND: part.GND, S1.pin_2, Tiras_de_LEDs_en_los_3_pisos.VSS, Piso_1.1, Buzzer.pin2, S2.pin_2, S3.pin_2, D1.cathode, U1.GND, IC1.GND
  N1: part.D2, Display_de_7_segmentos.Segment_E
  N2: part.D3, Display_de_7_segmentos.Segment_D
  N3: part.D4, Display_de_7_segmentos.Segment_C
  N4: part.D5, Display_de_7_segmentos.Segment_G
  N5: part.D6, S3.pin_1
  N6: part.D7, Display_de_7_segmentos.Segment_A
  N7: part.D8, Display_de_7_segmentos.Segment_B
  N8: part.D9, U1.IN2
  N9: part.D10, U1.IN1
  N10: part.D11/MOSI, D1.anode
  N11: part.D12/MISO, Tiras_de_LEDs_en_los_3_pisos.DIn
  N12: part.5V, Display_de_7_segmentos.common_anode, IC1.OUT
  N13: part.A5, S2.pin_1
  N14: part.A4, S1.pin_1
  N15: part.A3, Piso_1.2
  N16: part.A2, Piso_2.2
  N17: part.A0, Piso_3.2
  N18: part.D13/SCK, Buzzer.pin1
  N19: M1.pin_1, U1.OUT1
  N20: M1.pin_2, U1.OUT2
  12V: Tiras_de_LEDs_en_los_3_pisos.VDD, IC1.IN
  N21: Piso_2.1, Piso_3.1
